# Fritzing sketch geiger (saved by Fritzing 0.9.3b)
perfboards: 1

parts:
  Q1 = TRANSISTOR_NPN [package=to-92-ammo]
  U1 = V18ZA2P [package=v18za2p]
  5V = Power plug  # not connected
  Raspberry_Pi_1 = Raspberry Pi 3 [part_number=RPI-3-V1.2]  # not connected
  LED1 = LED - 5mm [color="Red (633nm)" package="5 mm [THT]"]  # not connected
  J1 = Piezo Speaker  # not connected
  200 = Resistor [tolerance=±5% resistance=220 package=THT]  # not connected
  10k = Resistor [tolerance=±5% resistance=220 package=THT]  # not connected
  10M = Resistor [tolerance=±5% resistance=220 package=THT]  # not connected
  GEIGER = Microphone  # not connected

nets:
  N1: Q1.E, U1.P$1
  N2: Q1.C, U1.P$2

notes:
  5V->400-500V
